# Fritzing sketch Ratoeira (saved by Fritzing 0.9.3b)
circuit board: 8.46667cm x 5.64444cm
breadboards: 1

parts:
  U1 = ESP8266 WiFi Module [part_number=ESP8266]
  R1 = Resistor [tolerance=±5% resistance=4.7k package=THT]
  C1 = Electrolytic Capacitor [capacitance=100µF package="100 mil [THT, electrolytic]"]
  R2 = Resistor [tolerance=±5% resistance=100 package=THT]
  U2 = TCRT5000 [package=THT]
  J1 = Screw terminal - 2 pins [package=THT]
  U3 = OMRON G3MB-202p [package=relay-s108t02]
  J2 = Screw terminal - 2 pins [package=THT]

nets:
  3.3V: U1.VCC, U1.CH_PD, R1.Pin_0, C1.+, R2.Pin_0, J1.pin1
  N1: U1.GPIO_0, U3.+
  N2: U1.GPIO_2, R1.Pin_1, U2.Pin_1
  GND: U1.GND, C1.-, U2.Pin_2, U2.Pin_3, J1.pin2, U3.-
  N3: R2.Pin_1, U2.Pin_4
  N4: U3.T1, J2.pin1
  N5: U3.T2, J2.pin2

custom parts:
  ESP8266 WiFi Module: Generic WiFi Module based on the ESP8266 with onboard PCB antenna and UART communications
  TCRT5000: TCRT5000 optical reflective sensor
  OMRON G3MB-202p: SPST SS relay
